# Fritzing sketch UniversalIRRemoteControl-v2 (saved by Fritzing 0.9.6b)

parts:
  WeMos_D1_Mini1 = WeMos D1 Mini
  IR3 = vs1838b [package=THT]
  R4 = Resistor [tolerance=±5% resistance=22 package="0402 [SMD]"]
  IC2 = Voltage Regulator LM1117 [package=sot223]
  C3 = Capacitor Polarized [part_number="10 µF" package=panasonic_c]
  C2 = Capacitor Polarized [part_number="10 µF" package=panasonic_c]
  U4 = USB connector [package=THT]
  Q1 = TRANSISTOR_NPN [part_number=S8050 package=to-92-ammo]
  D2 = LTE-302 [part_number=TSFF5210 package=lte-302]
  U5 = ESP-12F (ESP8266 WiFi Module) [part_number=ESP8266]

nets:
  N1: WeMos_D1_Mini1.3V3, IR3.Vs
  N2: WeMos_D1_Mini1.D4, IR3.Data
  N3: WeMos_D1_Mini1.G, IR3.GND
  N4: R4.Pin_0, Q1.E
  N5: R4.Pin_1, D2.A
  GND: IC2.ADJ, C3.-, C2.-, U4.GND, U4.chassis5, U4.chassis6, D2.C, U5.GND, U5.GPIO15
  N6: IC2.OUT, C2.+, U5.VCC, U5.EN
  N7: IC2.IN, C3.+, U4.5V, U4.d+, Q1.C
  N8: Q1.B, U5.GPIO13

notes:
  Gravador
  IR LED: 1,5V @ 100 mA
  Resistor: 12-15 Ω
  3V3
  5V

custom parts:
  ESP-12F (ESP8266 WiFi Module): WiFi Module based on the ESP8266 with onboard PCB antenna and UART communications
